# Fritzing sketch modelo (saved by Fritzing 0.9.3b)
breadboards: 1

parts:
  ARDUINO_UNO = Arduino Uno (Rev3)
  ZUMBADOR = Piezo Speaker
  LCD_16*2_I2C = LCD screen  # not connected
  LCM1602_IIC1 = LCM1602 IIC [part_number="LCM1602 IIC" chip_label="LCM1602 IIC" package="DIP (Dual Inline) [THT]"]
  LED1 = LED - 5mm [color="Red (633nm)" package="5 mm [THT]"]
  HUELLERO_ADAFRUITH = sensor_biometrico
  BLUETOOTH_HC-05 = Bluetooth HC-05 Macho
  TRANSISTOR_PNP = PNP-Transistor [package="TO92 [THT]"]
  R1 = Resistor [tolerance=±5% resistance=220 package=THT]
  LED2 = LED - 5mm [color="Red (633nm)" package="5 mm [THT]"]
  S1 = Pushbutton [package="[THT]"]  # not connected

nets:
  N1: ARDUINO_UNO.A4/SDA, LCM1602_IIC1.SDA
  N2: ARDUINO_UNO.A5/SCL, LCM1602_IIC1.SCL
  N3: ARDUINO_UNO.D8, R1.Pin_1, LED2.anode
  N4: ARDUINO_UNO.D0/RX, BLUETOOTH_HC-05.TXD
  N5: ARDUINO_UNO.D1/TX, BLUETOOTH_HC-05.RXD
  N6: ARDUINO_UNO.D3_PWM, HUELLERO_ADAFRUITH.RX
  N7: ARDUINO_UNO.D4, HUELLERO_ADAFRUITH.TX
  N8: ARDUINO_UNO.D5_PWM, ZUMBADOR.pin2
  N9: ARDUINO_UNO.D6_PWM, LED1.cathode
  N10: ARDUINO_UNO.RESET, TRANSISTOR_PNP.E
  3V3: ARDUINO_UNO.3V3, HUELLERO_ADAFRUITH.VCC
  VCC: ARDUINO_UNO.5V, LCM1602_IIC1.VCC, BLUETOOTH_HC-05.VCC
  GND: ARDUINO_UNO.GND, LCM1602_IIC1.GND, LED1.anode, HUELLERO_ADAFRUITH.GND, BLUETOOTH_HC-05.GND, TRANSISTOR_PNP.C, LED2.cathode
  N11: TRANSISTOR_PNP.B, R1.Pin_0

custom parts:
  LCM1602 IIC: I2C-Module to use a 1602 or 2004 LCD on with the wire.h libory Serial LCD Modul
  sensor_biometrico: Adafruit Optical Fingerprint Sensor
